# Fritzing sketch fritzing (saved by Fritzing 0.9.4)
circuit board: 8.46667cm x 5.64444cm
breadboards: 2

parts:
  U1 = ESP32-38PinWide [part_number=ESP32-38PinWide]
  R1 = Resistor [tolerance=±5% resistance=220 package="2512 [SMD]"]
  R2 = Resistor [tolerance=±5% resistance=220 package="2512 [SMD]"]
  R3 = Resistor [tolerance=±5% resistance=220 package="2512 [SMD]"]
  LED4 = RGB LED (com. cathode, rbg) [package="5 mm [THT]"]
  SP1 = SPEAKER [package=pcb_mount_speaker]
  R4 = Resistor [tolerance=±5% resistance=220 package="2512 [SMD]"]
  LCD1 = TFT 1.8 inch 160x128 w SD
  Part1 = Barometric Pressure Sensor - BMP180 Breakout (GY-68)
  HC-SR04_Sensor_1 = HC-SR04 Ultrasonic Distance Sensor

nets:
  N1: U1.GPIO32, HC-SR04_Sensor_1.ECHO
  N2: U1.GPIO33, HC-SR04_Sensor_1.TRIG
  N3: U1.GPIO26, R2.Pin_1
  N4: U1.GPIO27, R3.Pin_1
  N5: U1.GPIO12, R1.Pin_1
  GND: U1.GND, LED4.common_cathode, SP1.+, LCD1.GND, Part1.GND, HC-SR04_Sensor_1.GND
  VCC: U1.VIN, LCD1.VCC, Part1.VCC, HC-SR04_Sensor_1.VCC
  N6: U1.GPIO15, R4.Pin_0
  N7: U1.GPIO2, LCD1.RS/DC
  N8: U1.GPIO4, LCD1.RST
  N9: U1.GPIO16, LCD1.SD_CS
  N10: U1.GPIO5, LCD1.CS
  N11: U1.GPIO18, LCD1.CLK/SCK, LCD1.SD_SCK
  N12: U1.GPIO19, LCD1.SD_MISO
  N13: U1.GPIO21, Part1.SDA
  N14: U1.GPIO22, Part1.SCL
  N15: U1.GPIO23, LCD1.SDA/MOSI, LCD1.SD_MOSI
  N16: R1.Pin_0, LED4.red_anode
  N17: R2.Pin_0, LED4.green_anode
  N18: R3.Pin_0, LED4.blue_anode
  N19: SP1.-, R4.Pin_1

custom parts:
  ESP32-38PinWide: Generic 38-Pin ESP32 with wide format (only access to one side of pins on a breadboard) based on Stephen Lilley's HiLetgo ESP-WROOM-32 ESP32 ESP-32S Development Board.
  TFT 1.8 inch 160x128 w SD: This is a generic 1.8 tft spi lcd display available on ebay and others. The 1.8" display has 128x160 color pixels.
  HC-SR04 Ultrasonic Distance Sensor: The HC-SR04 is an ultrasonic distance sensor. It is capable of providing measurement for ranges of 2cm to 400cm. The module operates at 5V.
